# Fritzing sketch robot transporter rocketo (saved by Fritzing 0.9.3b)
perfboards: 1

parts:
  J1 = T-Connector Male [package=THT]
  J2 = T-Connector Female [package=THT]
  TRM1 = Terminal 2pin
  S1 = H-Bridge with L298N
  BAT1 = 18650 battery holder [package=battery-18650-kit]
  M1 = DOIT Esp32 DevKit v1 (30 pins long, 11 pins width) [part_number=ESP32S-PIN30]  # not connected
  M3 = DC Motor
  U2 = Voltage Regulator [package=to220-adj]
  C2 = Electrolytic Capacitor [capacitance=1μF package="0405 [SMD, electrolytic]"]
  C3 = Electrolytic Capacitor [capacitance=1μF package="0405 [SMD, electrolytic]"]
  M4 = DC Motor
  M5 = DC Motor
  M6 = DC Motor
  TRM2 = Terminal 2pin
  J3 = T-Connector Male [package=THT]
  J4 = T-Connector Female [package=THT]
  S2 = H-Bridge with L298N
  BAT2 = 18650 battery holder [package=battery-18650-kit]
  BAT3 = 18650 battery holder [package=battery-18650-kit]
  TRM3 = Terminal 2pin
  TRM4 = Terminal 2pin

nets:
  N1: J1.GND, BAT2.+
  N2: J1.VCC, BAT1.-
  N3: J2.GND, U2.IN, TRM4.pin_2
  N4: J2.VCC, C2.-, TRM4.pin_1
  GND: TRM1.pin_1, S1.GND, TRM2.pin_2, S2.GND
  5V: TRM1.pin_2, S1.5V, TRM2.pin_1, S2.5V
  N5: S1.M1-01, M3.pin_2
  N6: S1.M1-02, M3.pin_1
  N7: S1.M2-01, M4.pin_2
  N8: S1.M2-02, M4.pin_1
  N9: U2.ADJ, C2.+
  N10: U2.OUT, C3.-
  N11: M5.pin_1, S2.M2-02
  N12: M5.pin_2, S2.M2-01
  N13: M6.pin_1, S2.M1-02
  N14: M6.pin_2, S2.M1-01
  N15: J3.GND, BAT3.+
  N16: J3.VCC, BAT3.-
  N17: J4.GND, TRM3.pin_1
  N18: J4.VCC, TRM3.pin_2

custom parts:
  T-Connector Male: Red T - Male Connector for high current loads up to 60A.
  T-Connector Female: Red T - Female Connector for high current loads up to 60A.
  Terminal 2pin: 2-pin Terminal Block
  H-Bridge with L298N: h-bridge
  18650 battery holder: 18650 Battery Holder identical to the dual battery version.
  DOIT Esp32 DevKit v1 (30 pins long, 11 pins width): The DOIT Esp32 DevKit v1 is one of the development board created by DOIT to evaluate the ESP-WROOM-32 module. It is based on the ESP32 microcontroller that boasts Wifi, Bluetooth, Ethernet and Low Power support all in a single chip. (vanepp) made breadboard work, adjusted pin numbering and labels and reduced size of schematic and cleaned up pcb. This chip is 30pins long (2 x15) and 11 pins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
